// Logisim project ULA_8_BITS.circ as structural Verilog: 1 circuit, main circuit ULA_8BITS
module ULA_8BITS (
  input  [7:0] A,
  input  [7:0] B,
  input  [3:0] seletor,
  output [7:0] \saída 
);

  wire [7:0] and_1_out, nand_1_out, nor_1_out, not_1_out, or_1_out, shift_2_1_p2, shift_2_1_p3,
       somador_8_bits_1_p3, subtrator_1_p3, xor_1_out;

  assign or_1_out = A | B;  // OR_Gate or_1, 8 bits wide
  assign and_1_out = A & B;  // AND_Gate and_1, 8 bits wide
  assign not_1_out = ~A;  // NOT_Gate not_1, 8 bits wide
  assign xor_1_out = A ^ B;  // XOR_Gate xor_1, 8 bits wide
  // subtrator subtrator_1: pin names not known; wires that end beside it: A, B, subtrator_1_p3
  // shift_2 shift_2_1: pin names not known; wires that end beside it: A, shift_2_1_p2, shift_2_1_p3
  // somador_8_bits somador_8_bits_1: pin names not known; wires that end beside it: A, B, somador_8_bits_1_p3
  assign nor_1_out = ~(A | B);  // NOR_Gate nor_1, 8 bits wide
  assign nand_1_out = ~(A & B);  // NAND_Gate nand_1, 8 bits wide
  Multiplexer #(.select(4), .width(8)) multiplexer_1 (
    .in1(or_1_out), .in2(and_1_out), .in3(not_1_out), .in4(nor_1_out), .in5(nand_1_out), .in6(xor_1_out),
    .in7(subtrator_1_p3), .in8(shift_2_1_p2), .in9(shift_2_1_p3), .in10(somador_8_bits_1_p3), .out(\saída ),
    .sel(seletor));  // open: in0, in11, in12, in13, in14, in15, en

  // Notes on the sheet:
  //   SUB
  //   shift
  //   2 bits
  //   SUM
  //   OR
  //   AND
  //   NOT(A)
  //   NOR
  //   NAND
  //   XOR
  //   SUB
  //   SHIFT LEFT(A)
  //   SHIFT RIGHT(A)
  //   SOMADOR
  //   OPERAÇÕES
  //   0001
  //   0010
  //   0011
  //   0100
  //   0101
  //   0110
  //   0111
  //   1000
  //   1001
  //   1010
endmodule
